# Fritzing sketch Iot_project (saved by Fritzing 0.9.10b)
breadboards: 1

parts:
  U1 = LuaNode32 / ESP32
  부품1 = Soil Moisture Sensor
  DHT1 = Humidity and Temperature Sensor DHT11
  M1 = DC Motor [voltage_(max)=6V voltage_(min)=3V]
  MD03A1 = Dual VNH2SP30 Motor Driver [part_number=MD03A]

nets:
  N1: U1.D33, 부품1.SIG
  GND: U1.GND, 부품1.GND, DHT1.GND_2, MD03A1.GND
  VIN: U1.Vin, MD03A1.VIN
  3V3: U1.3V3, 부품1.VCC, DHT1.GND_1
  N2: U1.RX2, DHT1.Vcc
  N3: U1.D5, MD03A1.OUT_1A
  N4: M1.pin_2, MD03A1.+5V_(IN)

custom parts:
  LuaNode32 / ESP32: ESP32 based LuaNode32
  Humidity and Temperature Sensor DHT11: Digital relative humidity & temperature sensor DHT11
